# Fritzing sketch Design (saved by Fritzing 0.9.3b)
breadboards: 1

parts:
  U1 = STM32F40x [package="LQFP64, 10x10mm"]
  U9 = TJA1040 [package=so08]
  R1 = Resistor [tolerance=±5% resistance=120 package="1206 [SMD]"]
  R2 = Resistor [tolerance=±5% resistance=120 package="1206 [SMD]"]
  IC2 = Single-Chip USB to UART Bridge [package=mlp28]
  U10 = STM32F40x [package="LQFP64, 10x10mm"]
  U11 = TJA1040 [package=so08]
  IC3 = Single-Chip USB to UART Bridge [package=mlp28]
  U12 = STM32F40x [package="LQFP64, 10x10mm"]
  U13 = STM32F40x [package="LQFP64, 10x10mm"]
  U14 = TJA1040 [package=so08]
  U15 = TJA1040 [package=so08]
  IC4 = Single-Chip USB to UART Bridge [package=mlp28]
  IC5 = Single-Chip USB to UART Bridge [package=mlp28]

nets:
  GND: U1.VSS1, U9.GND, IC2.GND
  VCC: U1.VDD1, U9.VCC, IC2.VDD
  N1: U1.PA9, IC2.RXD
  N2: U1.PA10, IC2.TXD
  N3: U1.PA11, U9.RXD
  N4: U1.PA12, U9.TXD
  N5: U9.CANL, R1.Pin_0, R2.Pin_0, U11.CANL, U14.CANL, U15.CANL
  N6: U9.CANH, R1.Pin_1, R2.Pin_1, U14.CANH, U15.CANH
  GND_2: U10.VSS1, U11.GND, IC3.GND
  VCC_2: U10.VDD1, U11.VCC, IC3.VDD
  N7: U10.PA9, IC3.RXD
  N8: U10.PA10, IC3.TXD
  N9: U10.PA11, U11.RXD
  N10: U10.PA12, U11.TXD
  GND_3: U12.VSS1, U15.GND, IC4.GND
  VCC_3: U12.VDD1, U15.VCC, IC4.VDD
  N11: U12.PA9, IC4.RXD
  N12: U12.PA10, IC4.TXD
  N13: U12.PA11, U15.RXD
  N14: U12.PA12, U15.TXD
  GND_4: U13.VSS1, U14.GND, IC5.GND
  VCC_4: U13.VDD1, U14.VCC, IC5.VDD
  N15: U13.PA9, IC5.RXD
  N16: U13.PA10, IC5.TXD
  N17: U13.PA11, U14.RXD
  N18: U13.PA12, U14.TXD
